// Digital circuit Processador_Teste.dig as structural Verilog
module Processador_Teste (
  input  [4:0] A,
  input  [4:0] B,
  input  S,
  input  [31:0] A_2,
  input  [31:0] B_2,
  input  S_2,
  input  [31:0] in_9,
  input  [31:0] in_12,
  input  [31:0] in_13,
  input  [31:0] in_14,
  input  in_15,
  input  clk,
  input  [4:0] RegRd1,
  input  [4:0] RegRd2,
  input  [4:0] RegWr,
  input  [31:0] WrData,
  input  Write,
  input  rst,
  input  [4:0] RbAdd,
  input  clk_2,
  output [4:0] Y,
  output [31:0] Y_2,
  output [31:0] out_10,
  output [31:0] out_11,
  output [31:0] out_16,
  output [31:0] RdData1,
  output [31:0] RdData2,
  output [31:0] Rb
);

  MuX_2to1_5bits #(.applicationType("IVERILOG")) u_MuX_2to1_5bits (.A(A), .B(B), .S(S), .Y(Y));
  Mux_2to1_32bits #(.applicationType("IVERILOG")) u_Mux_2to1_32bits (.A(A_2), .B(B_2), .S(S_2), .Y(Y_2));
  Soma4 #(.applicationType("IVERILOG")) u_Soma4 (.A(in_9), .Y(out_10));
  somaPcDesvio #(.applicationType("IVERILOG")) u_somaPcDesvio (
    .endereco(in_12), .desvio(in_13), .enderecoDesvio(out_11));
  RegistradorPC #(.applicationType("IVERILOG")) u_RegistradorPC (.A(in_14), .Clk(clk), .Rst(in_15), .Y(out_16));
  BancoReg #(.applicationType("IVERILOG")) u_BancoReg (
    .RegRd1(RegRd1), .RegRd2(RegRd2), .RegWr(RegWr), .WrData(WrData), .Write(Write), .rst(rst), .clk(clk_2),
    .RbAdd(RbAdd), .RdData1(RdData1), .RdData2(RdData2), .Rb(Rb));

  // Notes on the sheet:
  //   in_15: default 1
  //   Write: default 1
endmodule

/* Code of MuX_2to1_5bits:
module MuX_2to1_5bits(A, B, S, Y);
	input wire [4:0] A, B;
	input wire S;
	output wire [4:0] Y;
	assign Y = S == 0 ? A : B;
endmodule;
*/

/* Code of Mux_2to1_32bits:
module Mux_2to1_32bits(A, B, S, Y);
	input wire [31:0] A, B;
	input wire S;
	output wire [31:0] Y;
	assign Y = S == 0 ? A : B;
endmodule;
*/

/* Code of Soma4:
module Soma4(input wire [31:0] A, output wire [31:0] Y);
	assign Y = A + 4;
endmodule;
*/

/* Code of somaPcDesvio:
module somaPcDesvio(endereco, desvio, enderecoDesvio);
	input wire [31:0] endereco, desvio;
	output wire [31:0] enderecoDesvio;
	assign enderecoDesvio = endereco + (desvio * 4);
endmodule;
*/

/* Code of RegistradorPC:
module RegistradorPC(input [31:0] A, input Clk, input Rst, output reg [31:0] Y);
	always @(posedge Clk) begin
		if(Rst == 0) begin	
			Y = 0;
		end else 
			Y = A;
	end;
endmodule;
*/

/* Code of BancoReg:
module BancoReg(RegRd1, RegRd2, RegWr, WrData, Write, rst, clk, RbAdd, RdData1, RdData2, Rb);
	input wire [4:0] RegRd1, RegRd2, RegWr;
	input wire [31:0] WrData;
	input wire Write, rst, clk;
	input [4:0] RbAdd;
	output wire [31:0] RdData1, RdData2, Rb;
	reg [31:0] registers [31:0];

	always @(posedge clk) begin
		if (rst) begin
      			for (integer i = 0; i < 32; i++) begin
        			registers[i] <= i;
      			end;
    		end
		else if (Write == 1) begin
			registers[RegWr] = WrData;
		end;
	end;
	
	assign RdData1 = registers[RegRd1];
	assign RdData2 = registers[RegRd2];
	assign Rb = registers[RbAdd];
endmodule;
*/
