// Digital circuit Template somaPcDesvio.dig as structural Verilog
module Template_somaPcDesvio (
  input  [31:0] endereco,
  input  [31:0] desvio,
  output [31:0] enderecoDesvio
);

  somaPcDesvio #(.applicationType("IVERILOG")) u_somaPcDesvio (
    .endereco(endereco), .desvio(desvio), .enderecoDesvio(enderecoDesvio));
endmodule

/* Test case somaPcDesvio:
endereco desvio enderecoDesvio
0       10	    40
100     (-5)          80
56	20	    136
32	(-8)	    0
*/

/* Code of somaPcDesvio:
module somaPcDesvio(endereco, desvio, enderecoDesvio);
	input wire [31:0] endereco, desvio;
	output wire [31:0] enderecoDesvio;
	assign enderecoDesvio = endereco + (desvio * 4);
endmodule;
*/
