// Digital circuit template BancoReg.dig as structural Verilog
module template_BancoReg (
  input  [4:0] RegRd1,
  input  [4:0] RegRd2,
  input  [4:0] RegWr,
  input  [31:0] WrData,
  input  Write,
  input  rst,
  input  clk,
  input  RbAdd,
  output [31:0] RdData2,
  output [31:0] RdData1,
  output [31:0] Rb
);

  BancoReg #(.applicationType("IVERILOG")) u_BancoReg (
    .RegRd1(RegRd1), .RegRd2(RegRd2), .RegWr(RegWr), .WrData(WrData), .Write(Write), .rst(rst), .clk(clk),
    .RbAdd(RbAdd), .RdData1(RdData1), .RdData2(RdData2), .Rb(Rb));
endmodule

/* Test case ULA:
	clk 	rst 	RegRd1     RegRd2 	RegWr 	WrData 	Write 	RdData1 	RdData2
	c    	0     	0        0      	0      	0     	0     	0       	0
	c    	1     	0        0      	0      	0     	0     	0       	0

loop(n,32)
     	c    	1     (n)     	(n)      	0     	0  	0   	(n)       	(n)
end loop
	c    	1     (0)    	(0)      	(0)     1   	1   	x       	x
loop(n,32)
	c    	1     (n)    	(n)      	(n)     (31-n)   1   	x       	x
end loop
loop(n,31)
	c    	1     (n)    	(n)      	(n)     0  	0  	(31-n)       	(31-n)
end loop
*/

/* Code of BancoReg:
module BancoReg( RegRd1, RegRd2, RegWr,  WrData, Write, rst,  clk, RbAdd, RdData1, RdData2, Rb);
	input wire [4:0] RegRd1, RegRd2, RegWr;
	input wire [31:0] WrData;
	input wire Write, rst, clk;
	input RbAdd;
	output wire [31:0] RdData1, RdData2, Rb;
	reg [31:0] registers [31:0];

	always @(posedge clk) begin
		if (Write == 1) begin
			registers[RegWr] = WrData;
		end;
	end;
	always @* begin

		if (rst) begin
      			for (integer i = 0; i < 32; i++) begin
        			registers[i] <= i;
      			end;
    		end
	end;
	
	assign RdData1 = registers[RegRd1];
	assign RdData2 = registers[RegRd2];
	assign Rb = registers[RbAdd];
endmodule
*/
