// Digital circuit template ULA.dig as structural Verilog
module template_ULA (
  input  [31:0] A,
  input  [31:0] B,
  input  [3:0] Op,
  output [31:0] Y,
  output Z
);

  ULA #(.applicationType("IVERILOG")) u_ULA (
    .operand1(A), .operand2(B), .ALU_control_vector(Op), .zero(Z), .ALU_result(Y));
endmodule

/* Test case ULA:
A B Op Z Y
 loop(i,5)
   let a = random(1<<32);
   let b = random(1<<32);
   (a) (b) 0 (ite((a & a)=0,1,0)) (a & b)
   (a) (b) 1 (ite((a | a)=0,1,0)) (a | b)
   (a) (b) 2 (ite((a + a)=0,1,0)) (a + b)
   (a) (b) 6 (ite((a - b)=0,1,0)) (a - b)
   (a) (a) 6 (ite((a - a)=0,1,0)) (a - a)
   (a) (b) 7 (ite((a < b)=0,1,0)) (a < b)
   
  end loop
*/

/* Code of ULA:
module ULA (operand1, operand2, ALU_control_vector, zero, ALU_result);
	input wire [31:0] operand1, operand2;
	input wire [3:0] ALU_control_vector;
	output reg zero;
	output [31:0] ALU_result;
	reg [31:0] out;
	always @* begin
		case (ALU_control_vector)
			4'b0000: out = operand1 & operand2; 
			4'b0001: out = operand1 | operand2;
			4'b0010: out = operand1 + operand2;
			4'b0110: out = operand1 - operand2;
			4'b0111: out = operand1 < operand2;
			4'b1100: out = !operand1 && !operand2;
		endcase;

		zero = out == 0;
	end;
	assign ALU_result = out;
endmodule
*/
