// Digital circuit template extensor.dig as structural Verilog
module template_extensor (
  input  [15:0] A,
  output [31:0] Y
);

  ExtensorSinal #(.applicationType("IVERILOG")) u_ExtensorSinal (.A(A), .Y(Y));
endmodule

/* Test case ULA:
A Y
 loop(i,10)
   let a = random(1<<16);
   (a) (signExt(16,a))
  end loop
*/

/* Code of ExtensorSinal:
module ExtensorSinal(A, Y);
   input [15:0] A;
   output [31:0] Y;
   assign Y = {{16{A[15]}}, A};
endmodule
*/
