// Digital circuit template mux2x1_5.dig as structural Verilog
module template_mux2x1_5 (
  input  [4:0] A,
  input  [4:0] B,
  input  S,
  output [4:0] Y
);

  Mux2x1_5bits #(.applicationType("IVERILOG")) u_Mux2x1_5bits (.A(A), .B(B), .S(S), .Y(Y));
endmodule

/* Test case mux5:
A B S Y
 loop(i,10)
   let a = random(1<<5);
   let b = random(1<<5);
   (a) (b) 0 (a)
   (a) (b) 1 (b)
  end loop
*/

/* Code of Mux2x1_5bits:
module Mux2x1_5bits( A, B, S, Y);
	input wire [4:0] A, B;
   	input wire S;
	output wire [4:0] Y;
	assign Y = S == 0 ? A : B;
endmodule
*/
