// Digital circuit template soma4.dig as structural Verilog
module template_soma4 (
  input  [31:0] endereco,
  output [31:0] novoEndereco
);

  Soma4 #(.applicationType("IVERILOG")) u_Soma4 (.A(endereco), .Y(novoEndereco));
endmodule

/* Test case somaPcDesvio:
endereco novoEndereco
 loop(i,10)
   let a = random(1<<16);
   (a) (a+4)
  end loop
*/

/* Code of Soma4:
module Soma4(input wire [31:0] A, output wire [31:0] Y);
	assign Y = A + 4;
endmodule;
*/
